// Logisim project ALU.circ as structural Verilog: 2 circuits, main circuit main
module main (
  input  in_1,
  input  [15:0] in_2,
  input  [15:0] in_3,
  input  [1:0] in_4,
  input  Add_Sub,
  output [15:0] out_6
);

  wire [15:0] adder_1_out, and_1_out, multiplexer_1_out, not_1_out, or_1_out, subtractor_1_out;

  assign and_1_out = in_2 & in_3;  // AND_Gate and_1, 16 bits wide
  assign or_1_out = in_2 | in_3;  // OR_Gate or_1, 16 bits wide
  assign not_1_out = ~in_3;  // NOT_Gate not_1, 16 bits wide
  Adder #(.width(16)) adder_1 (.a(in_2), .b(in_3), .out(adder_1_out), .cin(in_1));  // open: cout
  Subtractor #(.width(16)) subtractor_1 (.a(in_2), .b(in_3), .out(subtractor_1_out), .bin(in_1));  // open: bout
  Multiplexer #(.width(16)) multiplexer_1 (
    .in0(adder_1_out), .in1(subtractor_1_out), .out(multiplexer_1_out), .sel(Add_Sub));  // open: en
  Multiplexer #(.select(2), .width(16)) multiplexer_2 (
    .in0(and_1_out), .in1(or_1_out), .in2(not_1_out), .in3(multiplexer_1_out), .out(out_6), .sel(in_4));  // open: en

  // Notes on the sheet:
  //   A
  //   B
  //   C In
  //   Op Code
endmodule

module _1_bit_ALU (
  input  B_Invert,
  input  Op_1,
  input  Op_0,
  input  C_In,
  input  A,
  input  B,
  input  in_7,
  output out_8
);

  wire adder_1_out, and_1_out, multiplexer_1_out, not_1_out, or_1_out;

  Multiplexer multiplexer_1 (.in0(B), .in1(not_1_out), .out(multiplexer_1_out), .en(B_Invert));  // open: sel
  not not_1 (not_1_out, B);
  and and_1 (and_1_out, A, multiplexer_1_out);
  or or_1 (or_1_out, A, multiplexer_1_out);
  Adder #(.width(1)) adder_1 (.a(A), .b(multiplexer_1_out), .out(adder_1_out), .cin(C_In), .cout(in_7));
  Multiplexer #(.select(2)) multiplexer_2 (
    .in0(and_1_out), .in1(or_1_out), .in2(adder_1_out), .out(out_8), .en(Op_0));  // open: in3, sel

  assign Op_1 = Op_0;
endmodule
