// Logisim project IntroFSM.circ as structural Verilog: 1 circuit, main circuit main
module main (
  input  in_1,
  input  Input_1,
  input  Input_2,
  output out_4
);

  wire and_1_out, and_2_out, and_3_out, and_4_out, and_5_out, clock_1_out, d_ff_1_q, d_ff_2_q, not_1_out,
       not_2_out, not_3_out, not_4_out, or_1_out, or_2_out;

  not not_1 (not_1_out, Input_2);
  not not_2 (not_2_out, Input_1);
  not not_3 (not_3_out, d_ff_1_q);
  not not_4 (not_4_out, d_ff_2_q);
  and and_1 (and_1_out, not_3_out, d_ff_2_q, Input_2, Input_1);
  and and_2 (and_2_out, d_ff_1_q, not_4_out, not_2_out, Input_2);
  and and_3 (and_3_out, not_3_out, not_4_out, Input_1, not_1_out);
  and and_4 (and_4_out, d_ff_1_q, not_4_out, not_2_out, Input_2);
  and and_5 (and_5_out, d_ff_1_q, d_ff_2_q, Input_2, Input_1);
  and and_6 (out_4, d_ff_2_q, d_ff_1_q);
  Clock clock_1 (.out(clock_1_out));
  or or_1 (or_1_out, and_1_out, and_2_out);
  or or_2 (or_2_out, and_3_out, and_4_out, and_5_out);
  D_Flip_Flop d_ff_1 (.clk(clock_1_out), .D(or_1_out), .Q(d_ff_1_q), .preset(1'b0), .reset(in_1));  // open: Qn, en
  D_Flip_Flop d_ff_2 (.clk(clock_1_out), .D(or_2_out), .Q(d_ff_2_q), .preset(1'b0), .reset(in_1));  // open: Qn, en

  // Notes on the sheet:
  //   A
  //   B
  //   D1
  //   D0
  //   F
  //   A
  //   B
endmodule
