// Logisim project Vending_Machine.circ as structural Verilog: 1 circuit, main circuit main
module main (
  input  in_1,
  input  Q,
  input  D,
  input  N,
  output out_5
);

  wire and_1_out, and_2_out, and_3_out, and_4_out, and_5_out, and_6_out, and_7_out, and_8_out, and_9_out,
       and_10_out, and_11_out, and_12_out, and_13_out, and_14_out, and_15_out, and_16_out, clock_1_out,
       D0_out, D1_out, D2_out, d_ff_1_q, d_ff_2_q, d_ff_3_q, not_1_out, not_2_out, not_3_out, not_4_out,
       not_5_out, not_6_out;

  not not_1 (not_1_out, D);
  not not_2 (not_2_out, Q);
  not not_3 (not_3_out, N);
  not not_4 (not_4_out, d_ff_3_q);
  not not_5 (not_5_out, d_ff_2_q);
  not not_6 (not_6_out, d_ff_1_q);
  and and_1 (and_1_out, d_ff_3_q, not_5_out, not_2_out, N, not_1_out);
  and and_2 (and_2_out, not_4_out, Q, not_1_out, not_3_out);
  and and_3 (and_3_out, d_ff_3_q, not_5_out, Q, not_1_out, not_3_out);
  and and_4 (and_4_out, not_4_out, not_6_out, not_2_out, not_1_out, N);
  and and_5 (and_5_out, not_4_out, d_ff_1_q, not_2_out, D, not_3_out);
  and and_6 (and_6_out, d_ff_3_q, not_5_out, not_6_out, not_2_out, D, not_3_out);
  and and_7 (and_7_out, not_4_out, not_5_out, not_2_out, D, not_3_out);
  and and_8 (and_8_out, not_4_out, not_5_out, d_ff_1_q, not_2_out, not_1_out, N);
  and and_9 (and_9_out, not_4_out, d_ff_2_q, not_6_out, not_2_out, not_1_out, N);
  and and_10 (and_10_out, d_ff_3_q, not_5_out, d_ff_1_q, not_2_out, D, not_3_out);
  and and_11 (and_11_out, not_4_out, d_ff_2_q, d_ff_1_q, not_2_out, not_1_out, N);
  and and_12 (and_12_out, d_ff_3_q, not_5_out, not_6_out, not_2_out, not_1_out, N);
  and and_13 (and_13_out, d_ff_3_q, not_5_out, not_6_out, not_2_out, D, not_3_out);
  and and_14 (and_14_out, not_4_out, Q, not_1_out, not_3_out);
  and and_15 (and_15_out, d_ff_3_q, not_5_out, Q, not_1_out, not_3_out);
  and and_16 (and_16_out, not_4_out, d_ff_2_q, not_2_out, D, not_3_out);
  and and_17 (out_5, d_ff_3_q, not_5_out, d_ff_1_q);
  Clock clock_1 (.out(clock_1_out));
  or D0 (D0_out, and_1_out, and_2_out, and_3_out, and_4_out, and_5_out, and_6_out);
  or D1 (D1_out, and_7_out, and_8_out, and_9_out, and_10_out);
  or D2 (D2_out, and_11_out, and_12_out, and_13_out, and_14_out, and_15_out, and_16_out);
  D_Flip_Flop d_ff_1 (.clk(clock_1_out), .D(D0_out), .Q(d_ff_1_q), .preset(1'b0), .reset(in_1));  // open: Qn, en
  D_Flip_Flop d_ff_2 (.clk(clock_1_out), .D(D1_out), .Q(d_ff_2_q), .preset(1'b0), .reset(in_1));  // open: Qn, en
  D_Flip_Flop d_ff_3 (.clk(clock_1_out), .D(D2_out), .Q(d_ff_3_q), .preset(1'b0), .reset(in_1));  // open: Qn, en

  // Notes on the sheet:
  //   A
  //   B
  //   C
  //   D1
  //   D2
  //   F
  //   D0
  //   A
  //   B
  //   D0
  //   D1
  //   D2
  //   C
endmodule
