// Logisim project 16_bit_register_file.circ as structural Verilog: 1 circuit, main circuit main
module main (
);

  wire buffer_1_out, clock_out, control_p3, control_p4, control_p5, control_p6, fetch_decode_jump_p5,
       fetch_decode_jump_p6, fetch_decode_jump_p7, fetch_decode_jump_p8, fetch_decode_jump_p9, not_1_out;
  wire [11:0] fetch_decode_jump_p1;
  wire [15:0] alu_p5, fetch_decode_jump_p4, multiplexer_1_out, ram_1_data, ram_2_data, reg_file_p7;

  Clock clock (.out(clock_out));
  RAM #(.addrWidth(12), .dataWidth(16), .bus("separate")) ram_1 (
    .addr(fetch_decode_jump_p1), .data(ram_1_data));  // open: din, str, sel, clk, ld, clr
  // fetch_decode_jump_main fetch_decode_jump: pin names not known; wires that end beside it: fetch_decode_jump_p1, clock_out, ram_1_data, fetch_decode_jump_p4, fetch_decode_jump_p5, fetch_decode_jump_p6, fetch_decode_jump_p7, fetch_decode_jump_p8, fetch_decode_jump_p9
  // control_main control: pin names not known; wires that end beside it: fetch_decode_jump_p9, clock_out, control_p3, control_p4, control_p5, control_p6
  Multiplexer #(.width(16), .enable("false")) multiplexer_1 (
    .in0(ram_2_data), .in1(alu_p5), .out(multiplexer_1_out), .sel(control_p4));
  // _16_reg_file_main reg_file: pin names not known; wires that end beside it: multiplexer_1_out, fetch_decode_jump_p5, fetch_decode_jump_p6, fetch_decode_jump_p7, control_p3, control_p5, reg_file_p7, fetch_decode_jump_p4
  // alu_main alu: pin names not known; wires that end beside it: reg_file_p7, fetch_decode_jump_p4, fetch_decode_jump_p8, fetch_decode_jump_p9, alu_p5
  not not_1 (not_1_out, control_p6);
  buf buffer_1 (buffer_1_out, control_p6);
  RAM #(.addrWidth(16), .dataWidth(16), .bus("separate")) ram_2 (
    .addr(reg_file_p7), .din(fetch_decode_jump_p4), .data(ram_2_data), .clk(buffer_1_out), .ld(not_1_out));  // open: str, sel, clr
endmodule
