// Logisim project 16bitprocessor.circ as structural Verilog: 4 circuits, main circuit main
module main (
  input  in_1,
  input  [15:0] connect_me_to_test,
  input  in_3,
  output out_4
);

  wire alu_1_p5, clock_1_out, decode_1_branch, decode_1_constant__r7, decode_1_input__rt, decode_1_memtoreg,
       decode_1_output__rs, decode_1_use_immediate, decode_1_use_j_address, decode_1_use_pc___1,
       decode_1_write_enable, decode_1_write_to_rt, decode_1_writemem, keyboard_1_avail, registerfile_1_p6;
  wire [2:0] decode_1_rd, decode_1_rs, decode_1_rt, decode_1_shamt, multiplexer_3_out, registerfile_1_p3;
  wire [3:0] decode_1_op_code;
  wire [5:0] decode_1_immediate;
  wire [6:0] alu_1_p6_2;
  wire [8:0] alu_1_p6, not_1_out;
  wire [11:0] decode_1_jump_addr;
  wire [15:0] adder_1_out, alu_1_p2, bit_extender_1_out, bit_extender_2_out, multiplexer_1_out,
       multiplexer_6_out, multiplexer_7_out, PC_q, ram_1_data, registerfile_1_p7, rom_1_data;

  Multiplexer #(.width(16), .enable("false")) multiplexer_1 (
    .in0(adder_1_out), .in1({PC_q[15:12], decode_1_jump_addr}), .out(multiplexer_1_out),
    .sel(decode_1_use_j_address));
  Clock clock_1 (.out(clock_1_out));
  Register #(.width(16)) PC (.D(multiplexer_1_out), .en(1'b1), .Q(PC_q), .clk(clock_1_out));  // open: clr
  Keyboard keyboard_1 (
    .clk(clock_1_out), .re(decode_1_input__rt), .clr(in_1), .avail(keyboard_1_avail), .data(not_1_out[8:2]));
  Adder #(.width(16)) adder_1 (.a(16'h1), .b(PC_q), .out(adder_1_out), .cin(1'b0));  // open: cout
  ROM #(.addrWidth(16), .dataWidth(16)) rom_1 (.addr(PC_q), .data(rom_1_data));  // open: sel
  Multiplexer #(.width(16), .enable("false")) multiplexer_2 (
    .in0(multiplexer_6_out), .in1(adder_1_out), .sel(decode_1_use_pc___1));  // open: out
  Multiplexer #(.width(3), .enable("false")) multiplexer_3 (
    .in0(decode_1_rd), .in1(decode_1_rt), .out(multiplexer_3_out), .sel(decode_1_write_to_rt));
  decode decode_1 (
    .instruction(rom_1_data), .Write_Enable(decode_1_write_enable), .Write_to_Rt(decode_1_write_to_rt),
    .Use_Immediate(decode_1_use_immediate), .WriteMem(decode_1_writemem), .Branch(decode_1_branch),
    .MemtoReg(decode_1_memtoreg), .Use_J_Address(decode_1_use_j_address), .Use_PC___1(decode_1_use_pc___1),
    .Constant__r7(decode_1_constant__r7), .Output__rs(decode_1_output__rs), .Input__rt(decode_1_input__rt),
    .rs(decode_1_rs), .rt(decode_1_rt), .rd(decode_1_rd), .shamt(decode_1_shamt),
    .immediate(decode_1_immediate), .jump_addr(decode_1_jump_addr), .Op_code(decode_1_op_code));
  // RegisterFile registerfile_1: pin names not known; wires that end beside it: clock_1_out, decode_1_write_enable, registerfile_1_p3, decode_1_rs, decode_1_rt, registerfile_1_p6, registerfile_1_p7
  Multiplexer #(.width(3), .enable("false")) multiplexer_4 (
    .in0(multiplexer_3_out), .in1(3'b111), .out(registerfile_1_p3), .sel(decode_1_constant__r7));
  assign bit_extender_1_out = {{10{1'b0}}, decode_1_immediate};  // Bit_Extender bit_extender_1
  and branch (out_4, alu_1_p5, decode_1_branch);
  // ALU alu_1: pin names not known; wires that end beside it: registerfile_1_p6, alu_1_p2, decode_1_shamt, decode_1_op_code, alu_1_p5, {alu_1_p6_2, alu_1_p6}
  Multiplexer #(.width(16), .enable("false")) multiplexer_5 (
    .in0(registerfile_1_p7), .in1(bit_extender_1_out), .out(alu_1_p2), .sel(decode_1_use_immediate));
  TTY tty_1 (.data(alu_1_p6_2), .clk(clock_1_out), .we(decode_1_output__rs), .clr(in_3));
  RAM #(.addrWidth(16), .dataWidth(16), .bus("separate")) ram_1 (
    .addr({alu_1_p6_2, alu_1_p6}), .din(registerfile_1_p7), .data(ram_1_data), .str(decode_1_writemem),
    .clk(clock_1_out));  // open: sel, ld, clr
  Multiplexer #(.width(16), .enable("false")) multiplexer_6 (
    .in0(multiplexer_7_out), .in1(bit_extender_2_out), .out(multiplexer_6_out), .sel(decode_1_input__rt));
  Multiplexer #(.width(16), .enable("false")) multiplexer_7 (
    .in0({alu_1_p6_2, alu_1_p6}), .in1(ram_1_data), .out(multiplexer_7_out), .sel(decode_1_memtoreg));
  not not_1 (not_1_out[0], keyboard_1_avail);
  assign bit_extender_2_out = {{7{1'b0}}, {not_1_out[8:2], 1'b0, not_1_out[0]}};  // Bit_Extender bit_extender_2

  // Notes on the sheet:
  //   contents of rom_1 (hex, n*v repeats v):
  //   8d40 2048 620d 2080 5288 620d 2080 5288 6209 2081 5288 d07a d022 2041 3a68 9a80 2048 620d 20c0 52c8
  //   620d 20c6 52c8 6209 20c1 52c8 d07a 8a40 2081 1aa8 d039 208d f400 ac3f 2080 2101 7821 e040 781f 42d8
  //   a63c f200 20d8 6619 32c8 4318 a609 20c9 3658 4718 a605 641b 1490 14d0 1450 b025 c000 2100 20fe 1ae8
  //   20cf 9ac0 2081 7411 4450 58a0 5288 6821 6209 8ac0 a601 b05f 2081 3698 9ac0 20c4 9ac1 8ac1 a601 b03e
  //   2081 3698 9ac1 6824 208f 4510 20c5 34d0 20c1 7619 4698 a602 20c3 18e0 b04d 20c4 9ac1 2040 8ac1 a607
  //   a203 2058 6209 f200 2082 1aa8 c000 2081 3698 9ac1 6824 208f 4510 a202 a401 b062 20d8 6619 14d0 f400
  //   2041 b062 8280 a401 c000 f400 2081 1288 b07a
endmodule

module decode (
  input  [15:0] instruction,
  output Write_Enable,
  output Write_to_Rt,
  output Use_Immediate,
  output WriteMem,
  output Branch,
  output MemtoReg,
  output Use_J_Address,
  output Use_PC___1,
  output Constant__r7,
  output Output__rs,
  output Input__rt,
  output [2:0] rs,
  output [2:0] rt,
  output [2:0] rd,
  output [2:0] shamt,
  output [5:0] immediate,
  output [11:0] jump_addr,
  output [3:0] Op_code
);

  wire decoder_1_out1, decoder_1_out2, decoder_1_out3, decoder_1_out4, decoder_1_out5, decoder_1_out6,
       decoder_1_out7, decoder_1_out8, decoder_1_out9, decoder_1_out10, decoder_1_out11, decoder_1_out12,
       decoder_1_out13, decoder_1_out14, decoder_1_out15;

  Decoder #(.select(4), .enable("false")) decoder_1 (
    .out1(decoder_1_out1), .out2(decoder_1_out2), .out3(decoder_1_out3), .out4(decoder_1_out4),
    .out5(decoder_1_out5), .out6(decoder_1_out6), .out7(decoder_1_out7), .out8(decoder_1_out8),
    .out9(decoder_1_out9), .out10(decoder_1_out10), .out11(decoder_1_out11), .out12(decoder_1_out12),
    .out13(decoder_1_out13), .out14(decoder_1_out14), .out15(decoder_1_out15), .sel(instruction[15:12]));  // open: out0
  or or_1 (Write_Enable, decoder_1_out13, decoder_1_out1, decoder_1_out2, decoder_1_out3, decoder_1_out4, decoder_1_out5, decoder_1_out6, decoder_1_out7, decoder_1_out8, decoder_1_out14);
  buf or_2 (Output__rs, decoder_1_out15);  // OR_Gate
  or or_3 (Write_to_Rt, decoder_1_out14, decoder_1_out2, decoder_1_out8);
  or or_4 (Use_Immediate, decoder_1_out2, decoder_1_out13, decoder_1_out11);
  buf or_5 (Input__rt, decoder_1_out14);  // OR_Gate
  buf or_6 (WriteMem, decoder_1_out9);  // OR_Gate
  buf or_7 (Branch, decoder_1_out10);  // OR_Gate
  buf or_8 (MemtoReg, decoder_1_out8);  // OR_Gate
  or or_9 (Use_J_Address, decoder_1_out11, decoder_1_out13);
  buf or_10 (Use_PC___1, decoder_1_out13);  // OR_Gate
  or or_11 (Constant__r7, decoder_1_out13, decoder_1_out12);

  assign immediate = instruction[5:0];
  assign jump_addr = instruction[11:0];
  assign Op_code = instruction[15:12];
  assign rd = instruction[5:3];
  assign rs = instruction[11:9];
  assign rt = instruction[8:6];
  assign shamt = instruction[2:0];

  // Notes on the sheet:
  //   Output: 0 Constant
  //   Output 1 add
  //   Output 2: ldi
  //   Output 3: sub
  //   Output 4: and
  //   Output 5: xor
  //   Output 6: rotl
  //   Output 7: rotr
  //   Output 8: lw
  //   Output 9: sw
  //   Output 10: bnez
  //   Output 11: j L
  //   Output 12: ret
  //   Output 13: jal L
  //   Output 14: input $rt
  //   Output 15: output $rs
  //   R Type
  //   I Type
  //   J Type
endmodule

module ALU (
  input  carry,
  input  [15:0] S_Register,
  input  [15:0] T_Register_Immediate,
  input  [3:0] Op_Code,
  input  [2:0] shamt,
  output [15:0] Normal_Output
);

  wire [3:0] bit_extender_1_out;
  wire [15:0] adder_1_out, and_1_out, shifter_1_out, shifter_2_out, subtractor_1_out, xor_1_out;

  assign bit_extender_1_out = {{1{1'b0}}, shamt};  // Bit_Extender bit_extender_1
  Adder #(.width(16)) adder_1 (.a(S_Register), .b(T_Register_Immediate), .out(adder_1_out));  // open: cin, cout
  Subtractor #(.width(16)) subtractor_1 (
    .a(S_Register), .b(T_Register_Immediate), .out(subtractor_1_out));  // open: bin, bout
  assign and_1_out = S_Register & T_Register_Immediate;  // AND_Gate and_1, 16 bits wide
  assign xor_1_out = S_Register ^ T_Register_Immediate;  // XOR_Gate xor_1, 16 bits wide
  Shifter #(.width(16), .shift("rl")) shifter_1 (.in(S_Register), .\dist (bit_extender_1_out), .out(shifter_1_out));
  Shifter #(.width(16), .shift("rr")) shifter_2 (.in(S_Register), .\dist (bit_extender_1_out), .out(shifter_2_out));
  Multiplexer #(.select(4), .width(16)) multiplexer_1 (
    .in1(adder_1_out), .in2(T_Register_Immediate), .in3(subtractor_1_out), .in4(and_1_out), .in5(xor_1_out),
    .in6(shifter_1_out), .in7(shifter_2_out), .in8(S_Register), .in9(T_Register_Immediate),
    .in10(S_Register), .in14(T_Register_Immediate), .in15(S_Register), .out(Normal_Output), .sel(Op_Code));  // open: in0, in11, in12, in13, en

  // Notes on the sheet:
  //   Output: 0 Constant
  //   Output 1 add
  //   Output 2: ldi
  //   Output 3: sub
  //   Output 4: and
  //   Output 5: xor
  //   Output 6: rotl
  //   Output 7: rotr
  //   Output 8: lw
  //   Output 9: sw
  //   Output 10: bnez
  //   Output 11: j L
  //   Output 12: ret
  //   Output 13: jal L
  //   Output 14: input $rt
  //   Output 15: output $rs
endmodule

module test_Decoder (
  input  [15:0] instruction,
  output reg_write_en,
  output ALUSrc,
  output register_destination,
  output MemtoReg,
  output MemWrite,
  output Branch,
  output use_j_address,
  output [2:0] rs,
  output [2:0] rt,
  output [2:0] rd,
  output [2:0] shamt,
  output [5:0] immediate,
  output [11:0] jump_addr,
  output [3:0] Op_code
);

  wire decoder_1_out1, decoder_1_out2, decoder_1_out3, decoder_1_out4, decoder_1_out5, decoder_1_out6,
       decoder_1_out7, decoder_1_out8, decoder_1_out9, decoder_1_out10, decoder_1_out11, decoder_1_out12,
       decoder_1_out13, li_out;

  Decoder #(.select(4), .enable("false")) decoder_1 (
    .out1(decoder_1_out1), .out2(decoder_1_out2), .out3(decoder_1_out3), .out4(decoder_1_out4),
    .out5(decoder_1_out5), .out6(decoder_1_out6), .out7(decoder_1_out7), .out8(decoder_1_out8),
    .out9(decoder_1_out9), .out10(decoder_1_out10), .out11(decoder_1_out11), .out12(decoder_1_out12),
    .out13(decoder_1_out13), .sel(instruction[15:12]));  // open: out0, out14, out15
  or R_Type (register_destination, decoder_1_out1, decoder_1_out3, decoder_1_out4, decoder_1_out5, decoder_1_out6, decoder_1_out7, decoder_1_out12);
  buf li (li_out, decoder_1_out2);  // OR_Gate
  buf lw (MemtoReg, decoder_1_out8);  // OR_Gate
  buf sw (MemWrite, decoder_1_out9);  // OR_Gate
  buf bnez (Branch, decoder_1_out10);  // OR_Gate
  or jump (use_j_address, decoder_1_out11, decoder_1_out13);
  or or_1 (reg_write_en, register_destination, li_out, MemtoReg);
  or or_2 (ALUSrc, li_out, MemtoReg, MemWrite);

  assign immediate = instruction[5:0];
  assign jump_addr = instruction[11:0];
  assign Op_code = instruction[15:12];
  assign rd = instruction[5:3];
  assign rs = instruction[11:9];
  assign rt = instruction[8:6];
  assign shamt = instruction[2:0];

  // Notes on the sheet:
  //   Output: 0 Constant
  //   Output 1 add
  //   Output 2: ldi
  //   Output 3: sub
  //   Output 4: and
  //   Output 5: xor
  //   Output 6: rotl
  //   Output 7: rotr
  //   Output 8: lw
  //   Output 9: sw
  //   Output 10: bnez
  //   Output 11: j L
  //   Output 12: ret
  //   Output 13: jal L
  //   Output 14: input $rt
  //   Output 15: output $rs
  //   R Type
  //   I Type
  //   J Type
endmodule
