// Logisim project 8_bit_CPU.circ as structural Verilog: 2 circuits, main circuit main
module main (
  input  [7:0] connect_me_to_test
);

  wire clock_1_out, decode_1_reg_write_en, decode_1_use_immediate, decode_1_use_j_addr,
       decode_1_use_val_from_mem, decode_1_write_to_rt;
  wire [1:0] decode_1_rd, decode_1_rs, decode_1_rt, multiplexer_2_out;
  wire [5:0] decode_1_jump_addr;
  wire [7:0] adder_1_out, adder_2_out, decode_1_immediate, multiplexer_1_out, multiplexer_3_out, PC_q,
       registerfile_1_p1, registerfile_1_p7, registerfile_1_p8, rom_1_data, rom_2_data;

  Clock clock_1 (.out(clock_1_out));
  Register PC (.D(multiplexer_1_out), .en(1'b1), .Q(PC_q), .clk(clock_1_out));  // open: clr
  Multiplexer #(.width(8), .enable("false")) multiplexer_1 (
    .in0(adder_1_out), .in1({PC_q[7:6], decode_1_jump_addr}), .out(multiplexer_1_out),
    .sel(decode_1_use_j_addr));
  Adder adder_1 (.a(8'h1), .b(PC_q), .out(adder_1_out), .cin(1'b0));  // open: cout
  ROM rom_1 (.addr(PC_q), .data(rom_1_data));  // open: sel
  decode decode_1 (
    .instruction(rom_1_data), .reg_write_en(decode_1_reg_write_en), .write_to_rt(decode_1_write_to_rt),
    .use_immediate(decode_1_use_immediate), .use_val_from_mem(decode_1_use_val_from_mem),
    .use_j_addr(decode_1_use_j_addr), .rs(decode_1_rs), .rt(decode_1_rt), .rd(decode_1_rd),
    .immediate(decode_1_immediate), .jump_addr(decode_1_jump_addr));
  Multiplexer #(.width(2), .enable("false")) multiplexer_2 (
    .in0(decode_1_rd), .in1(decode_1_rt), .out(multiplexer_2_out), .sel(decode_1_write_to_rt));
  // RegisterFile registerfile_1: pin names not known; wires that end beside it: registerfile_1_p1, clock_1_out, decode_1_reg_write_en, multiplexer_2_out, decode_1_rs, decode_1_rt, registerfile_1_p7, registerfile_1_p8
  Multiplexer #(.width(8), .enable("false")) multiplexer_3 (
    .in0(registerfile_1_p8), .in1(decode_1_immediate), .out(multiplexer_3_out), .sel(decode_1_use_immediate));
  Multiplexer #(.width(8), .enable("false")) multiplexer_4 (
    .in0(adder_2_out), .in1(rom_2_data), .out(registerfile_1_p1), .sel(decode_1_use_val_from_mem));
  Adder adder_2 (.a(registerfile_1_p7), .b(multiplexer_3_out), .out(adder_2_out), .cin(1'b0));  // open: cout
  ROM rom_2 (.addr(adder_2_out), .data(rom_2_data));  // open: sel

  // Notes on the sheet:
  //   contents of rom_1 (hex, n*v repeats v):
  //   4f 0 0 4f 0 7f
  //   contents of rom_2 (hex, n*v repeats v):
  //   11 22 33 44 55 66 77 88 99 aa bb cc dd ee ff
endmodule

module decode (
  input  [7:0] instruction,
  output reg_write_en,
  output write_to_rt,
  output use_immediate,
  output use_val_from_mem,
  output use_j_addr,
  output [1:0] rs,
  output [1:0] rt,
  output [1:0] rd,
  output [7:0] immediate,
  output [5:0] jump_addr
);

  wire decoder_1_out0, decoder_1_out1;

  Decoder #(.select(2), .enable("false")) decoder_1 (
    .out0(decoder_1_out0), .out1(decoder_1_out1), .out2(use_val_from_mem), .out3(use_j_addr),
    .sel(instruction[7:6]));
  or or_1 (reg_write_en, decoder_1_out0, decoder_1_out1, use_val_from_mem);
  or or_2 (write_to_rt, decoder_1_out1, use_val_from_mem);
  or or_3 (use_immediate, decoder_1_out1, use_val_from_mem);

  assign immediate = {{6{1'b0}}, instruction[1:0]};
  assign jump_addr = instruction[5:0];
  assign rd = instruction[1:0];
  assign rs = instruction[5:4];
  assign rt = instruction[3:2];
endmodule
