// Logisim project fetch-decode-jump.circ as structural Verilog: 1 circuit, main circuit main
module main (
  input  [15:0] instruction_output,
  input  clock,
  input  [15:0] zero_register,
  output [3:0] reg_0,
  output [3:0] reg_1,
  output [3:0] reg_2,
  output [7:0] immediate,
  output [11:0] address_input,
  output [3:0] opcode
);

  wire and_1_out, comparator_1_eq, jump_out, jump_zero_out, not_1_out, not_2_out, not_3_out, not_4_out,
       or_1_out;
  wire [11:0] adder_1_out, adder_2_out, bit_extender_1_out, multiplexer_1_out, multiplexer_2_out,
       multiplexer_3_out;

  Register #(.width(12)) register_1 (.D(multiplexer_1_out), .Q(address_input), .clk(clock));  // open: en, clr
  Multiplexer #(.width(12), .enable("false")) multiplexer_1 (
    .in0(multiplexer_2_out), .in1(multiplexer_3_out), .out(multiplexer_1_out), .sel(or_1_out));
  Multiplexer #(.width(12), .enable("false")) multiplexer_2 (
    .in0(adder_1_out), .in1(zero_register[11:0]), .out(multiplexer_2_out), .sel(and_1_out));
  Adder #(.width(12)) adder_1 (.a(address_input), .b(12'h1), .out(adder_1_out));  // open: cin, cout
  Multiplexer #(.width(12), .enable("false")) multiplexer_3 (
    .in0(adder_2_out), .in1(instruction_output[11:0]), .out(multiplexer_3_out), .sel(instruction_output[12]));
  Adder #(.width(12)) adder_2 (.a(bit_extender_1_out), .b(address_input), .out(adder_2_out));  // open: cin, cout
  and and_1 (and_1_out, not_2_out, not_1_out, instruction_output[13], instruction_output[12]);
  not not_1 (not_1_out, instruction_output[14]);
  not not_2 (not_2_out, instruction_output[15]);
  not not_3 (not_3_out, instruction_output[13]);
  and jump (jump_out, not_2_out, not_1_out, not_3_out, instruction_output[12]);
  or or_1 (or_1_out, jump_out, jump_zero_out);
  not not_4 (not_4_out, instruction_output[12]);
  and jump_zero (jump_zero_out, not_2_out, not_1_out, instruction_output[13], not_4_out, comparator_1_eq);
  Comparator #(.width(16)) comparator_1 (.a({16{1'b0}}), .b(zero_register), .eq(comparator_1_eq));  // open: gt, lt
  assign bit_extender_1_out = {{4{instruction_output[11]}}, instruction_output[11:4]};  // Bit_Extender bit_extender_1

  assign immediate = instruction_output[7:0];
  assign opcode = instruction_output[15:12];
  assign reg_0 = instruction_output[11:8];
  assign reg_1 = instruction_output[7:4];
  assign reg_2 = instruction_output[3:0];
endmodule
